# Fritzing sketch Discharger (saved by Fritzing 0.9.3b)
circuit board: 21.1526cm x 13.9114cm

parts:
  Part1 = Arduino Nano (Rev3.0)
  S1 = Pushbutton [package="[THT]"]
  S2 = Pushbutton [package="[THT]"]
  U1 = LIPO-1000mAh [package=lipo-1000]
  U2 = LIPO-1000mAh [package=lipo-1000]
  U3 = LIPO-1000mAh [package=lipo-1000]
  U4 = LIPO-1000mAh [package=lipo-1000]
  U5 = LIPO-1000mAh [package=lipo-1000]
  U6 = LIPO-1000mAh [package=lipo-1000]
  LCD1 = LCD screen
  R1_10Ω_5W1 = Resistor [tolerance=±5% resistance=10 power=5W package=THT]
  R1_10Ω_5W2 = Resistor [tolerance=±5% resistance=10 power=5W package=THT]
  R1_10Ω_5W3 = Resistor [tolerance=±5% resistance=10 power=5W package=THT]
  R1_10Ω_5W5 = Resistor [tolerance=±5% resistance=10 power=5W package=THT]
  R1_10Ω_5W = Resistor [tolerance=±5% resistance=10 power=5W package=THT]
  U7 = Mini-USB _B_ connector with 5th pin broken out. [package=usb-micro_b]
  S3 = Round Pushbutton
  R1_10Ω_5W4 = Resistor [tolerance=±5% resistance=10 power=5W package=THT]
  KY-1 = Keyes Relay [package=THT]
  KY-2 = Keyes Relay [package=THT]
  KY-3 = Keyes Relay [package=THT]
  KY-4 = Keyes Relay [package=THT]
  KY-5 = Keyes Relay [package=THT]
  KY-6 = Keyes Relay [package=THT]
  LCM1602_IIC1 = LCM1602 IIC [part_number="LCM1602 IIC" chip_label="LCM1602 IIC" package="DIP (Dual Inline) [THT]"]
  C1 = Electrolytic Capacitor [capacitance=10µF package="100 mil [THT, electrolytic]"]
  R2 = Resistor [tolerance=±5% resistance=10k package=THT]
  R1 = Resistor [tolerance=±5% resistance=100k package=THT]
  C2 = Electrolytic Capacitor [capacitance=10µF package="100 mil [THT, electrolytic]"]
  R3 = Resistor [tolerance=±5% resistance=100k package=THT]
  R4 = Resistor [tolerance=±5% resistance=10k package=THT]
  C3 = Electrolytic Capacitor [capacitance=10µF package="100 mil [THT, electrolytic]"]
  R5 = Resistor [tolerance=±5% resistance=100k package=THT]
  R6 = Resistor [tolerance=±5% resistance=10k package=THT]
  C4 = Electrolytic Capacitor [capacitance=10µF package="100 mil [THT, electrolytic]"]
  R7 = Resistor [tolerance=±5% resistance=100k package=THT]
  R8 = Resistor [tolerance=±5% resistance=10k package=THT]
  C5 = Electrolytic Capacitor [capacitance=10µF package="100 mil [THT, electrolytic]"]
  R9 = Resistor [tolerance=±5% resistance=10k package=THT]
  R10 = Resistor [tolerance=±5% resistance=100k package=THT]
  C6 = Electrolytic Capacitor [capacitance=10µF package="100 mil [THT, electrolytic]"]
  R11 = Resistor [tolerance=±5% resistance=10k package=THT]
  R12 = Resistor [tolerance=±5% resistance=100k package=THT]

nets:
  N1: Part1.D3, S2.Pin_2
  GND: Part1.D4, Part1.GND, S1.Pin_3, S1.Pin_4, S2.Pin_3, S2.Pin_4, U1.-, U2.-, U3.-, U4.-, U5.-, U6.-, R1_10Ω_5W1.Pin_1, R1_10Ω_5W2.Pin_1, R1_10Ω_5W3.Pin_1, R1_10Ω_5W5.Pin_1, R1_10Ω_5W.Pin_1, U7.GND, R1_10Ω_5W4.Pin_1, KY-1.ground, KY-2.ground, KY-3.ground, KY-4.ground, KY-5.ground, KY-6.ground, LCM1602_IIC1.GND, C1.+, R1.Pin_1, C2.+, R3.Pin_1, C3.+, R5.Pin_1, C4.+, R7.Pin_1, C5.+, R10.Pin_1, C6.+, R12.Pin_1
  N2: Part1.D5, KY-5.signal
  N3: Part1.D6, KY-6.signal
  N4: Part1.D7, KY-4.signal
  N5: Part1.D8, KY-3.signal
  N6: Part1.D9, KY-2.signal
  N7: Part1.D10, KY-1.signal
  5V: Part1.5V, S3.leg0, KY-1.power, KY-2.power, KY-3.power, KY-4.power, KY-5.power, KY-6.power, LCM1602_IIC1.VCC
  N8: Part1.A7, C6.-, R11.Pin_1, R12.Pin_0
  N9: Part1.A6, C5.-, R9.Pin_1, R10.Pin_0
  N10: Part1.A5, LCM1602_IIC1.SCL
  N11: Part1.A4, LCM1602_IIC1.SDA
  N12: Part1.A3, C4.-, R7.Pin_0, R8.Pin_1
  N13: Part1.A2, C3.-, R5.Pin_0, R6.Pin_1
  N14: Part1.A1, C2.-, R3.Pin_0, R4.Pin_1
  N15: Part1.A0, C1.-, R2.Pin_1, R1.Pin_0
  N16: U1.+, KY-1.C, R2.Pin_0
  N17: U2.+, KY-2.C, R4.Pin_0
  N18: U3.+, KY-3.C, R6.Pin_0
  N19: U4.+, KY-4.C, R8.Pin_0
  N20: U5.+, KY-6.C, R9.Pin_0
  N21: U6.+, KY-5.C, R11.Pin_0
  VSS: LCD1.VSS, LCM1602_IIC1.VSS
  VDD: LCD1.VDD, LCM1602_IIC1.VDD
  N22: LCD1.V0, LCM1602_IIC1.V0
  N23: LCD1.RS, LCM1602_IIC1.RS
  N24: LCD1.R/W, LCM1602_IIC1.RW
  N25: LCD1.E, LCM1602_IIC1.E
  N26: LCD1.DB0, LCM1602_IIC1.D0
  N27: LCD1.DB1, LCM1602_IIC1.D1
  N28: LCD1.DB2, LCM1602_IIC1.D2
  N29: LCD1.DB3, LCM1602_IIC1.D3
  N30: LCD1.DB4, LCM1602_IIC1.D4
  N31: LCD1.DB5, LCM1602_IIC1.D5
  N32: LCD1.DB6, LCM1602_IIC1.D6
  N33: LCD1.DB7, LCM1602_IIC1.D7
  N34: LCD1.LED+, LCM1602_IIC1.A
  N35: LCD1.LED-, LCM1602_IIC1.K
  N36: R1_10Ω_5W1.Pin_0, KY-2.NO
  N37: R1_10Ω_5W2.Pin_0, KY-3.NO
  N38: R1_10Ω_5W3.Pin_0, KY-4.NO
  N39: R1_10Ω_5W5.Pin_0, KY-6.NO
  N40: R1_10Ω_5W.Pin_0, KY-1.NO
  N41: U7.VBUS, S3.leg1
  N42: R1_10Ω_5W4.Pin_0, KY-5.NO
  N43: LCM1602_IIC1.LED_A, LCM1602_IIC1.LED_B

custom parts:
  Keyes Relay: The Keyes 5V relay module is suitable for SCM development, home appliance control. It uses a 5V~12V TIL control signal which can control DC / AC signal.
  LCM1602 IIC: I2C-Module to use a 1602 or 2004 LCD on with the wire.h libory Serial LCD Modul
